# Fritzing sketch schematic (saved by Fritzing 0.9.3b)
breadboards: 1

parts:
  U1 = ESP32-38PinWide [part_number=ESP32-38PinWide]
  C1 = Capacitor Polarized [package=cpol-radial-100uf-25v]
  GY-NEO6MV3 = SUP500F [package=sup500f]

nets:
  N1: U1.3.3, GY-NEO6MV3.VCC
  N2: U1.EN, C1.+
  GND: U1.GND, GY-NEO6MV3.GND
  N3: U1.GPIO11, C1.-
  N4: U1.GPIO16, GY-NEO6MV3.TX-O
  N5: U1.GPIO17, GY-NEO6MV3.RX-I

custom parts:
  ESP32-38PinWide: Generic 38-Pin ESP32 with wide format (only access to one side of pins on a breadboard) based on Stephen Lilley's HiLetgo ESP-WROOM-32 ESP32 ESP-32S Development Board.
